// Logisim project DigitDisplay.circ as structural Verilog
module DigitPlay_7Seg_Naive (
  input  in_1,
  input  in_2,
  input  in_3,
  input  in_4
);

  wire and_1_out, and_2_out, and_3_out, and_4_out, and_5_out, and_6_out, and_7_out, and_8_out, and_9_out,
       and_10_out, and_11_out, and_12_out, and_13_out, and_14_out, and_15_out, and_16_out, and_17_out,
       b0000_out, b0001_out, b0010_out, b0011_out, b0100_out, b0101_out, b0110_out, b0111_out, b1000_out,
       b1001_out, Dec0_out, Dec1_out, Dec2_out, Dec3_out, Dec4_out, Dec5_out, Dec6_out, Dec7_out, Dec8_out,
       nand_1_out, not_1_out, not_2_out, not_3_out, not_4_out, not_5_out, OFF2_out, OFF14_out, OFF017_out,
       OFF56_out, OFF147_out, OFF1237_out, ON0268_out, or_1_out, or_2_out, or_3_out, or_4_out, or_5_out,
       or_6_out, or_7_out;

  not not_1 (not_1_out, in_1);
  not not_2 (not_2_out, in_2);
  and b0000 (b0000_out, not_1_out, not_2_out);
  and b0001 (b0001_out, in_1, not_2_out);
  and b0010 (b0010_out, not_1_out, in_2);
  and b0011 (b0011_out, in_1, in_2);
  and b0100 (b0100_out, not_1_out, not_2_out);
  and b0101 (b0101_out, in_1, not_2_out);
  and b0110 (b0110_out, not_1_out, in_2);
  and b0111 (b0111_out, in_1, in_2);
  and b1000 (b1000_out, not_1_out, not_2_out);
  and b1001 (b1001_out, in_1, not_2_out);
  not not_3 (not_3_out, in_3);
  and and_1 (and_1_out, b0000_out, not_3_out);
  and and_2 (and_2_out, b0001_out, not_3_out);
  and and_3 (and_3_out, b0010_out, not_3_out);
  and and_4 (and_4_out, b0011_out, not_3_out);
  and and_5 (and_5_out, b0100_out, in_3);
  and and_6 (and_6_out, b0101_out, in_3);
  and and_7 (and_7_out, b0110_out, in_3);
  and and_8 (and_8_out, b0111_out, in_3);
  and and_9 (and_9_out, b1000_out, not_3_out);
  and and_10 (and_10_out, b1001_out, not_3_out);
  not not_4 (not_4_out, in_4);
  and Dec0 (Dec0_out, and_1_out, not_4_out);
  and Dec1 (Dec1_out, and_2_out, not_4_out);
  and Dec2 (Dec2_out, and_3_out, not_4_out);
  and Dec3 (Dec3_out, and_4_out, not_4_out);
  and Dec4 (Dec4_out, and_5_out, not_4_out);
  and Dec5 (Dec5_out, and_6_out, not_4_out);
  and Dec6 (Dec6_out, and_7_out, not_4_out);
  and Dec7 (Dec7_out, and_8_out, not_4_out);
  and Dec8 (Dec8_out, and_9_out, in_4);
  // AND_Gate Dec9 has open pins: in0=and_10_out, in1=in_4, out=open
  or or_1 (or_1_out, in_2, in_3);
  nand nand_1 (nand_1_out, or_1_out, in_4);
  or or_2 (or_2_out, Dec1_out, Dec2_out);
  or or_3 (or_3_out, Dec3_out, Dec7_out);
  or or_4 (or_4_out, Dec0_out, Dec1_out);
  or or_5 (or_5_out, Dec0_out, Dec2_out);
  or or_6 (or_6_out, Dec6_out, Dec8_out);
  or or_7 (or_7_out, Dec1_out, Dec4_out);
  nor OFF56 (OFF56_out, Dec5_out, Dec6_out);
  nor OFF14 (OFF14_out, Dec1_out, Dec4_out);
  nor OFF1237 (OFF1237_out, or_2_out, or_3_out);
  nor OFF017 (OFF017_out, or_4_out, Dec7_out);
  or ON0268 (ON0268_out, or_5_out, or_6_out);
  nor OFF147 (OFF147_out, or_7_out, Dec7_out);
  not OFF2 (OFF2_out, Dec2_out);
  and and_11 (and_11_out, OFF56_out, nand_1_out);
  and and_12 (and_12_out, OFF14_out, nand_1_out);
  and and_13 (and_13_out, OFF1237_out, nand_1_out);
  and and_14 (and_14_out, OFF017_out, nand_1_out);
  and and_15 (and_15_out, ON0268_out, nand_1_out);
  and and_16 (and_16_out, OFF147_out, nand_1_out);
  and and_17 (and_17_out, OFF2_out, nand_1_out);
  _7_Segment_Display u_7_segment_display_1 (
    .g(and_14_out), .f(and_13_out), .a(and_12_out), .b(and_11_out), .e(and_15_out), .d(and_16_out),
    .c(and_17_out), .dp(not_5_out));
  not not_5 (not_5_out, nand_1_out);
endmodule

module DigitPlay_Hex (
  input  b1,
  input  in_2,
  input  in_3,
  input  in_4
);

  wire and_1_out, and_2_out, and_3_out, and_4_out, and_5_out, and_6_out, and_7_out, and_8_out, b00_out,
       b0x_out, b0xx_out, b0xxx_out, b01_out, b10_out, b11_out, not_1_out, undriven, undriven_2, undriven_3,
       undriven_4, undriven_5, undriven_6, undriven_7, undriven_8;

  not not_1 (not_1_out, b1);
  not b0x (b0x_out, in_2);
  and b00 (b00_out, not_1_out, b0x_out);
  and b01 (b01_out, b1, b0x_out);
  and b10 (b10_out, not_1_out, in_2);
  and b11 (b11_out, b1, in_2);
  not b0xx (b0xx_out, in_3);
  and and_1 (and_1_out, b00_out, b0xx_out);
  and and_2 (and_2_out, b01_out, b0xx_out);
  and and_3 (and_3_out, b10_out, b0xx_out);
  and and_4 (and_4_out, b11_out, b0xx_out);
  and and_5 (and_5_out, b00_out, in_3);
  and and_6 (and_6_out, b01_out, in_3);
  and and_7 (and_7_out, b10_out, in_3);
  and and_8 (and_8_out, b11_out, in_3);
  not b0xxx (b0xxx_out, in_4);
  // AND_Gate and_9 has open pins: in0=and_1_out, in1=b0xxx_out, out=open
  // AND_Gate and_10 has open pins: in0=and_2_out, in1=b0xxx_out, out=open
  // AND_Gate and_11 has open pins: in0=and_3_out, in1=b0xxx_out, out=open
  // AND_Gate and_12 has open pins: in0=and_4_out, in1=b0xxx_out, out=open
  // AND_Gate and_13 has open pins: in0=and_5_out, in1=b0xxx_out, out=open
  // AND_Gate and_14 has open pins: in0=and_6_out, in1=b0xxx_out, out=open
  // AND_Gate and_15 has open pins: in0=and_7_out, in1=b0xxx_out, out=open
  // AND_Gate and_16 has open pins: in0=and_8_out, in1=b0xxx_out, out=open
  // AND_Gate and_17 has open pins: in0=and_1_out, in1=in_4, out=open
  // AND_Gate and_18 has open pins: in0=and_2_out, in1=in_4, out=open
  // AND_Gate and_19 has open pins: in0=and_3_out, in1=in_4, out=open
  // AND_Gate and_20 has open pins: in0=and_4_out, in1=in_4, out=open
  // AND_Gate and_21 has open pins: in0=and_5_out, in1=in_4, out=open
  // AND_Gate and_22 has open pins: in0=and_6_out, in1=in_4, out=open
  // AND_Gate and_23 has open pins: in0=and_7_out, in1=in_4, out=open
  // AND_Gate and_24 has open pins: in0=and_8_out, in1=in_4, out=open
  _7_Segment_Display u_7_segment_display_1 (
    .g(undriven), .f(undriven_3), .a(undriven_5), .b(undriven_7), .e(undriven_2), .d(undriven_4),
    .c(undriven_6), .dp(undriven_8));

  // Notes on the sheet:
  //   b0
  //   b1x
  //   b1xx
  //   b1xx
endmodule
