// Logisim project IO.circ as structural Verilog: 1 circuit, main circuit main
module main (
  input  in_1,
  input  in_2,
  input  in_3,
  input  in_4,
  input  in_5,
  input  in_6,
  input  [6:0] in_7,
  input  in_8,
  input  in_9,
  input  in_10,
  input  in_11,
  input  in_12,
  input  in_13,
  input  Clear,
  input  in_15,
  output [6:0] out_16
);

  wire keyboard_1_avail, keyboard_2_avail;
  wire [6:0] keyboard_1_data;

  // RGBLED rgbled_1: pin names not known; wires that end beside it: in_5, in_4, in_6
  Keyboard keyboard_1 (.clk(in_10), .re(in_13), .clr(in_11), .avail(keyboard_1_avail), .data(keyboard_1_data));
  Keyboard keyboard_2 (.clk(in_1), .re(in_3), .clr(in_2), .avail(keyboard_2_avail), .data(out_16));
  TTY tty_1 (.data(in_7), .we(in_9), .clr(in_8));  // open: clk
  LED led_1 (.in(keyboard_1_avail));
  LED led_2 (.in(keyboard_1_avail));
  LED led_3 (.in(keyboard_2_avail));
  LED led_4 (.in(keyboard_2_avail));
  TTY tty_2 (.data(keyboard_1_data), .clk(in_12), .we(in_15), .clr(Clear));

  // Notes on the sheet:
  //   Wrong
endmodule
