// Logisim project Logisim_tut.circ as structural Verilog: 1 circuit, main circuit main
module main (
  input  x,
  input  y,
  input  Wiring_Pin_e,
  output o,
  output Pin_Output
);

  wire And1_out, And2_out, and_1_out, DFF_D_FlipFlop_Mem_qn, not_1_out, not_2_out, not_3_out;

  not not_1 (not_1_out, y);
  not not_2 (not_2_out, x);
  and And1 (And1_out, x, not_1_out);
  and And2 (And2_out, not_2_out, y);
  or Or1 (o, And1_out, And2_out);
  not not_3 (not_3_out, Wiring_Pin_e);
  and and_1 (and_1_out, not_3_out, Wiring_Pin_e);
  D_Flip_Flop DFF_D_FlipFlop_Mem (
    .D(DFF_D_FlipFlop_Mem_qn), .clk(and_1_out), .Q(Pin_Output), .Qn(DFF_D_FlipFlop_Mem_qn));  // open: preset, reset
endmodule
