// Logisim project _DMX24.circ as structural Verilog
module DMX24 (
  input  in_1,
  input  in_2,
  input  in_3,
  output out_4,
  output out_5,
  output out_6,
  output out_7
);

  wire and_1_out, and_2_out, and_3_out, and_4_out, not_1_out, not_2_out;

  not not_1 (not_1_out, in_1);
  not not_2 (not_2_out, in_2);
  and and_1 (and_1_out, not_1_out, not_2_out);
  and and_2 (and_2_out, in_1, not_2_out);
  and and_3 (and_3_out, not_1_out, in_2);
  and and_4 (and_4_out, in_1, in_2);
  and and_5 (out_4, and_1_out, in_3);
  and and_6 (out_5, and_2_out, in_3);
  and and_7 (out_6, and_3_out, in_3);
  and and_8 (out_7, and_4_out, in_3);
endmodule

module DMX38 (
  input  in_1,
  input  in_2,
  input  in_3,
  output out_4,
  output out_5,
  output out_6,
  output out_7,
  output out_8,
  output out_9,
  output out_10,
  output out_11
);

  wire not_1_out;

  not not_1 (not_1_out, in_3);
  DMX24 dmx24_1 (
    .in_1(in_1), .in_2(in_2), .in_3(not_1_out), .out_4(out_4), .out_5(out_5), .out_6(out_6), .out_7(out_7));
  DMX24 dmx24_2 (.in_1(in_1), .in_2(in_2), .in_3(in_3), .out_4(out_8), .out_5(out_9), .out_6(out_10), .out_7(out_11));
endmodule
